// Logisim project  2 Bit Arithmetic Unit in Logisim.circ as structural Verilog: 1 circuit, main circuit main
module main (
  input  CIN,
  input  A0,
  input  B0,
  input  in_4,
  input  in_5,
  input  A1,
  input  B1,
  input  in_8,
  input  in_9,
  input  [1:0] select_bits,
  output D0,
  output D1,
  output cout
);

  wire adder_1_cout, multiplexer_1_out, multiplexer_2_out, not_1_out, not_2_out;

  not not_1 (not_1_out, B1);
  not not_2 (not_2_out, B0);
  Multiplexer #(.select(2)) multiplexer_1 (
    .in0(B0), .in1(not_2_out), .in2(in_4), .in3(in_5), .out(multiplexer_1_out), .sel(select_bits));  // open: en
  Multiplexer #(.select(2)) multiplexer_2 (
    .in0(B1), .in1(not_1_out), .in2(in_8), .in3(in_9), .out(multiplexer_2_out), .sel(select_bits));  // open: en
  Adder #(.width(1)) adder_1 (.a(A0), .b(multiplexer_1_out), .out(D0), .cin(CIN), .cout(adder_1_cout));
  Adder #(.width(1)) adder_2 (.a(A1), .b(multiplexer_2_out), .out(D1), .cin(adder_1_cout), .cout(cout));
endmodule
